# Fritzing sketch circuit (saved by Fritzing 0.9.8b)
breadboards: 1

parts:
  Mod1 = ESP32 - CAM
  Battery = 4 x AAA Battery Mount [part_number="(5.0V - 5.2V)"]
  CDS = PHOTOCELL [part_number="12k - 58k o-mu / 10Lux" package=photocell-kit]
  Switch = Pushbutton [package="[SMD]"]
  Toggle_Switch = Taiway 100-SP-X-T1 SPDT Miniature Toggle Switch [part_number="(Battery ON OFF)" package=THT]
  Resistor = Resistor [tolerance=±1% resistance=22k power=0.25 package=THT]
  Capacitor = Ceramic Capacitor [capacitance="100 nF" voltage=35V package="0805 [SMD, multilayer]"]

nets:
  N1: Mod1.5V, Toggle_Switch.L2, Resistor.Pin_0, Capacitor.0
  N2: Mod1.GND, Battery.-, CDS.P$2, Switch.Pin_1, Switch.Pin_2, Capacitor.1
  N3: Mod1.IO12, CDS.P$1, Resistor.Pin_1
  N4: Mod1.IO2, Switch.Pin_3, Switch.Pin_4
  N5: Battery.+, Toggle_Switch.L1

custom parts:
  ESP32 - CAM: The ESP32-CAM has a very competitive small-size camera module that can operate independently as a minimum system with a footprint of only 27*40.5*4.5mm and a deep sleep current of up to 6mA.
